# Fritzing sketch SimonSays (saved by Fritzing 0.9.3b)
breadboards: 1

parts:
  Raspberry_Pi_1 = Raspberry Pi 3 [part_number=RPI-3-V1.2]
  LED1 = LED - 5mm [color="Green (555nm)" package="5 mm [THT]"]
  LED2 = smd LED [color="Blue (430nm)" package="0603 [SMD]"]
  LED2_2 = smd LED [color="Red (633nm)" package="0805 [SMD]"]
  LED3 = LED - 5mm [color="Yellow (585nm)" package="5 mm [THT]"]
  LED4 = RGB LED (com. cathode, rgb) [package="5 mm [THT]"]
  R1 = Resistor [tolerance=±5% resistance=220 package=THT]
  R2 = Resistor [tolerance=±5% resistance=220 package=THT]
  R3 = Resistor [tolerance=±5% resistance=220 package=THT]
  R4 = Resistor [tolerance=±5% resistance=220 package=THT]
  R5 = Resistor [tolerance=±5% resistance=220 package=THT]
  R6 = Resistor [tolerance=±5% resistance=220 package=THT]
  R7 = Resistor [tolerance=±5% resistance=220 package=THT]
  R8 = Resistor [tolerance=±5% resistance=220 package=THT]
  SG1 = Buzzer 12mm [package=buzzer-12mm-ns-kit]
  S1 = Pushbutton [package="[THT]"]
  S2 = Pushbutton [package="[THT]"]
  S3 = Pushbutton [package="[THT]"]
  S4 = Pushbutton [package="[THT]"]

nets:
  N1: Raspberry_Pi_1.GIPO21, SG1.1
  N2: Raspberry_Pi_1.GIPO20, LED1.cathode
  N3: Raspberry_Pi_1.GIPO16, LED2.cathode
  N4: Raspberry_Pi_1.GND, SG1.2, S1.Pin_3, S1.Pin_4, S2.Pin_3, S2.Pin_4, S3.Pin_3, S3.Pin_4, S4.Pin_3, S4.Pin_4
  N5: Raspberry_Pi_1.GIPO12, LED2_2.cathode
  N6: Raspberry_Pi_1.GIPO7, LED3.cathode
  N7: Raspberry_Pi_1.GIPO8, R5.Pin_1, S2.Pin_1, S2.Pin_2
  N8: Raspberry_Pi_1.GIPO25, R3.Pin_1, S3.Pin_1, S3.Pin_2
  N9: Raspberry_Pi_1.GIPO24, R4.Pin_1, S4.Pin_1, S4.Pin_2
  N10: Raspberry_Pi_1.GIPO23, R2.Pin_1, S1.Pin_1, S1.Pin_2
  N11: Raspberry_Pi_1.GIPO18, R7.Pin_1
  N12: Raspberry_Pi_1.GIPO15, R8.Pin_1
  N13: Raspberry_Pi_1.GIPO14, R6.Pin_1
  N14: LED1.anode, R4.Pin_0
  N15: LED2.anode, R2.Pin_0
  N16: LED2_2.anode, R3.Pin_0
  N17: LED3.anode, R5.Pin_0
  N18: LED4.red_anode, R6.Pin_0
  N19: LED4.common_cathode, R1.Pin_0
  N20: LED4.green_anode, R7.Pin_0
  N21: LED4.blue_anode, R8.Pin_0
